# Fritzing sketch Fritzing_circuit_diagram (saved by Fritzing 0.9.3b)
breadboards: 2

parts:
  Bauteil2 = Bluetooth HC-05 Macho
  M1 = DC Motor
  M2 = DC Motor
  Bauteil3 = Arduino Uno (Rev3) - ICSP
  U1 = LIPO-1000mAh [package=lipo-1000]
  CPU1 = NodeMCU WROOM ESP 32
  U2 = LIPO-1000mAh [package=lipo-1000]
  GY1 = MPU-6050 Board GY-521 [form="♀ (female)" package=THT]
  L298N1 = L298N DC motor driver
  J1 = Basic Servo
  R1 = Resistor [tolerance=±5% resistance=100 package=THT]
  R2 = Resistor [tolerance=±5% resistance=220 package=THT]
  S2 = Pushbutton [package="[SMD]"]
  R3 = Resistor [tolerance=±5% resistance=220 package="0805 [SMD]"]
  U3 = LIPO-1000mAh [package=lipo-1000]
  U4 = LIPO-1000mAh [package=lipo-1000]

nets:
  N1: Bauteil2.TXD, R1.Pin_0, R2.Pin_1
  N2: Bauteil2.RXD, Bauteil3.D1/TX
  VCC: Bauteil2.VCC, Bauteil3.5V
  GND: Bauteil2.GND, Bauteil3.GND, U2.+, U2.-, L298N1.GND, J1.gnd, R2.Pin_0, U3.-
  N3: M1.pin_1, L298N1.OUT2
  N4: M1.pin_2, L298N1.OUT1
  N5: M2.pin_1, L298N1.OUT4
  N6: M2.pin_2, L298N1.OUT3
  N7: Bauteil3.D8, L298N1.IN1
  N8: Bauteil3.D9_PWM, L298N1.IN2
  N9: Bauteil3.D10_PWM/SS, L298N1.IN3
  N10: Bauteil3.D11_PWM/MOSI, L298N1.IN4
  N11: Bauteil3.D0/RX, R1.Pin_1
  N12: Bauteil3.D3_PWM, J1.pulse
  N13: Bauteil3.D5_PWM, L298N1.ENA
  N14: Bauteil3.D6_PWM, L298N1.ENB
  N15: Bauteil3.VIN, U3.+
  N16: U1.+, U4.-
  N17: CPU1.pin_8, CPU1.pin_24, CPU1.pin_28
  N18: CPU1.pin_9, CPU1.pin_25, S2.Pin_3, S2.Pin_4, R3.Pin_1
  N19: CPU1.pin_17, GY1.pin1, S2.Pin_1, S2.Pin_2
  N20: CPU1.pin_18, GY1.pin2, R3.Pin_0
  N21: CPU1.pin_27, GY1.pin4
  N22: CPU1.pin_30, GY1.pin3
  N23: L298N1.12V, U4.+
  5V: L298N1.5V, J1.vcc

custom parts:
  NodeMCU WROOM ESP 32: 30 pol Development Kit
  MPU-6050 Board GY-521: Acelerometro y Giroscopio MPU-6050 Board GY-521
  L298N DC motor driver: 2x DC motor driver with 78M05 positive voltage regulator (7..35 V) L298N: max 46 V, 2 A Set 5 V Enable jumper to enable 5 V regultor (needed for the L298N) and +5 V output at screw terminal or supply external +5 V at screw terminal Set ENA and/or ENB to +5 V to enable motor permanently or supply ENA and/or ENB with PWM signal IN1 and IN2 set rotation directory for motor A (OUT1/OUT2) IN2 and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
